// Digital circuit FP_Adder.dig as structural Verilog
module FP_Adder (
  input  [31:0] B,
  input  [31:0] A,
  input  Sel
);

  wire Exponent_Difference_c_o;
  wire [7:7] undriven, undriven_2;
  wire [26:0] Exponent_Difference_s, multiplexer_1_out, multiplexer_2_out;

  Sub #(.Bits(8)) Exponent_Difference (
    .a(B[30:23]), .b(A[30:23]), .c_i(1'b0), .s(Exponent_Difference_s[7:0]), .c_o(Exponent_Difference_c_o));
  Multiplexer #(.Bits(23)) multiplexer_1 (
    .sel(Exponent_Difference_c_o), .in_0(A[22:0]), .in_1(B[22:0]), .out(multiplexer_1_out[22:0]));
  Multiplexer #(.Bits(23)) multiplexer_2 (
    .sel(Exponent_Difference_c_o), .in_0(B[22:0]), .in_1(A[22:0]), .out(multiplexer_2_out[22:0]));
  Multiplexer #(.Bits(8)) multiplexer_3 (.sel(Exponent_Difference_c_o), .in_0(B[30:23]), .in_1(A[30:23]));  // open: out
  BarrelShifter #(.Bits(35), .direction("right")) barrelshifter_1 (
    .in({undriven[7], {7{1'b0}}, multiplexer_1_out}), .shift({undriven[7], {7{1'b0}}, Exponent_Difference_s}));  // open: out
  Multiplexer multiplexer_4 (.sel(Sel), .in_0(B[31]), .in_1(A[31]));  // open: out
  // Pins of 8 and 27 bits meet at Exponent_Difference_s
  // Pins of 23 and 27 bits meet at multiplexer_1_out
  // Pins of 23 and 27 bits meet at multiplexer_2_out
  // Pins of 7 and 8 bits meet at {undriven[7], {7{1'b0}}}
  // Pins of 7 and 8 bits meet at {undriven_2[7], {7{1'b0}}}

  // Notes on the sheet:
  //   FP Adder
endmodule
